# Fritzing sketch DATN (saved by Fritzing 0.9.9b)

parts:
  MH-ET_LIVE_ESP32_DEVKIT1 = MH-ET LIVE ESP32 DEVKIT 38 pins
  Part1 = InvenSense MPU6050
  SIM800L1 = SIM800L
  Part3 = RFID-RC522-v3
  U1 = SUP500F [package=sup500f]
  microSD1 = MicroSD Card Module
  M1 = 1 chan 5v relay module
  M2 = 1 chan 5v relay module
  J1 = Piezo Speaker
  S1 = Round Pushbutton
  U2 = SWITCH-SPST-2 [package=switch-spst-vertical]
  R2 = Resistor [tolerance=±5% power=0.25 resistance=220 package=THT]
  LED2 = LED - 5mm [color="Red (633nm)" current=0.030 package="5 mm [THT]"]
  R1 = Resistor [tolerance=±5% power=0.25 resistance=220 package=THT]
  LED3 = LED - 5mm [color="Red (633nm)" current=0.030 package="5 mm [THT]"]
  LED4 = LED - 5mm [color="Red (633nm)" current=0.030 package="5 mm [THT]"]
  LED5 = LED - 5mm [color="Red (633nm)" current=0.030 package="5 mm [THT]"]
  MH-ET_LIVE_ESP32_DEVKIT2 = MH-ET LIVE ESP32 DEVKIT 38 pins
  Part4 = InvenSense MPU6050
  J2 = Piezo Speaker
  LED6 = LED - 5mm [color="Red (633nm)" current=0.030 package="5 mm [THT]"]
  LED7 = LED - 5mm [color="Red (633nm)" current=0.030 package="5 mm [THT]"]
  S2 = Toggle Switch [package=THT]
  U3 = LIPO-1000mAh [package=lipo-1000]
  TP1 = TP4056 [chip_label=TP4056 package="DIP (Dual Inline) [THT]"]

nets:
  VCC: MH-ET_LIVE_ESP32_DEVKIT1.3V3, Part1.VCC, Part3.3.3V, U1.VCC
  N1: MH-ET_LIVE_ESP32_DEVKIT1.IO35, M1.pin_5, U2.P
  N2: MH-ET_LIVE_ESP32_DEVKIT1.IO32, SIM800L1.RST, SIM800L1.RXD
  N3: MH-ET_LIVE_ESP32_DEVKIT1.IO33, SIM800L1.TXD
  N4: MH-ET_LIVE_ESP32_DEVKIT1.IO25, LED5.anode
  N5: MH-ET_LIVE_ESP32_DEVKIT1.IO26, Part1.SCL
  N6: MH-ET_LIVE_ESP32_DEVKIT1.IO27, Part1.SDA
  N7: MH-ET_LIVE_ESP32_DEVKIT1.IO14, LED3.anode
  N8: MH-ET_LIVE_ESP32_DEVKIT1.IO12, LED2.anode
  GND: MH-ET_LIVE_ESP32_DEVKIT1.GND#58, Part1.GND, SIM800L1.GND, M1.pin_2, M2.pin_2, LED2.cathode, R1.Pin_0, LED3.cathode, LED4.cathode, LED5.cathode
  N9: MH-ET_LIVE_ESP32_DEVKIT1.IO13, LED4.anode
  5V: MH-ET_LIVE_ESP32_DEVKIT1.5V, microSD1.VCC, M1.pin_1, M2.pin_1
  GND_2: MH-ET_LIVE_ESP32_DEVKIT1.GND#64, Part3.GND, microSD1.GND
  N10: MH-ET_LIVE_ESP32_DEVKIT1.IO23, Part3.MOSI, microSD1.MOSI
  N11: MH-ET_LIVE_ESP32_DEVKIT1.IO22, Part3.RST
  N12: MH-ET_LIVE_ESP32_DEVKIT1.IO21, Part3.SDA
  N13: MH-ET_LIVE_ESP32_DEVKIT1.GND#70, U1.GND, J1.pin1
  N14: MH-ET_LIVE_ESP32_DEVKIT1.IO19, Part3.MISO, Part3.IRQ, microSD1.MISO
  N15: MH-ET_LIVE_ESP32_DEVKIT1.IO18, Part3.SCK, microSD1.SCK
  N16: MH-ET_LIVE_ESP32_DEVKIT1.IO5, microSD1.CS
  N17: MH-ET_LIVE_ESP32_DEVKIT1.IO17, U1.RX-I
  N18: MH-ET_LIVE_ESP32_DEVKIT1.IO16, U1.TX-O
  N19: MH-ET_LIVE_ESP32_DEVKIT1.IO4, M1.pin_3
  N20: MH-ET_LIVE_ESP32_DEVKIT1.IO2, M2.pin_3
  N21: MH-ET_LIVE_ESP32_DEVKIT1.IO15, J1.pin2
  N22: SIM800L1.NET, SIM800L1.VCC
  N23: M1.pin_6, S1.leg0
  N24: M2.pin_6, U2.O
  N25: R2.Pin_0, R1.Pin_1
  3V3: MH-ET_LIVE_ESP32_DEVKIT2.3V3, Part4.VCC
  N26: MH-ET_LIVE_ESP32_DEVKIT2.IO26, Part4.SCL
  N27: MH-ET_LIVE_ESP32_DEVKIT2.IO27, Part4.SDA
  N28: MH-ET_LIVE_ESP32_DEVKIT2.GND#58, Part4.GND, U3.-, TP1.pin5, TP1.pin6
  N29: MH-ET_LIVE_ESP32_DEVKIT2.5V, S2.L2
  N30: MH-ET_LIVE_ESP32_DEVKIT2.GND#70, J2.pin1, LED6.cathode, LED7.cathode
  N31: MH-ET_LIVE_ESP32_DEVKIT2.IO18, J2.pin2
  N32: MH-ET_LIVE_ESP32_DEVKIT2.IO17, LED6.anode
  N33: MH-ET_LIVE_ESP32_DEVKIT2.IO16, LED7.anode
  N34: S2.COM, TP1.pin3
  N35: U3.+, TP1.pin4

custom parts:
  MH-ET LIVE ESP32 DEVKIT 38 pins: http://mh.nodebb.com/topic/2/mh-et-live-esp32-devkit
  SIM800L: SIM800L is a miniature cellular module which allows for GPRS transmission, sending and receiving SMS and making and receiving voice calls. Low cost and small footprint and quad band frequency support make this module perfect solution for any project that require long range connectivity. After connecting power module boots up, searches for cellular network and login automatically. On board LED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
  RFID-RC522-v3: A simple China made RFID-RC522 Reader (6x4 cm); do check the pin labels, as this is a MFRC522 based clone.
  SUP500F: SUP500F Venus GPS
  MicroSD Card Module: A common microSD card module.
  1 chan 5v relay module: 1 Channel 5V Relay Module Board Shield with Optocoupler Support High and Low Level Trigger for Arduino.
  TP4056: A DIP stand-in part for whatever IC you want. With 6 pins on a 300mil dual inline package (DIP) footprint.
